# Fritzing sketch i2C_128x32_Uno (saved by Fritzing 0.9.0b)

parts:
  Part1 = Arduino Uno (Rev3)
  OLED1 = 128x32 I2C Monochrome OLED Display

nets:
  N1: Part1.A4/SDA, OLED1.SDA
  N2: Part1.A5/SCL, OLED1.SCL
  3V3: Part1.3V3, OLED1.3.3V
  GND: Part1.GND, OLED1.GND
